# Fritzing sketch victoria (saved by Fritzing 0.9.2b)
circuit board: 8.46667cm x 5.64444cm
breadboards: 2

parts:
  Part1 = Arduino Mega 2560 (Rev3)
  Q1 = MOSFET-NCHANNEL [package=to-92]
  DS2 = DS18B20 1-Wire Temperature Sensor [part_number=DS18B20]
  RTC = Real Time Clock Module - DS1307 RTC Breakout Board
  Q2 = MOSFET-NCHANNEL [package=to-92]
  Q3 = MOSFET-NCHANNEL [package=to-92]
  Q4 = MOSFET-NCHANNEL [package=to-92]
  Q5 = MOSFET-NCHANNEL [package=to-92]
  R6 = Resistor [tolerance=±5% resistance=10k package=THT]
  R7 = Resistor [tolerance=±5% resistance=10k package=THT]
  R8 = Resistor [tolerance=±5% resistance=10k package=THT]
  R9 = Resistor [tolerance=±5% resistance=100 package=THT]
  R10 = Resistor [tolerance=±5% resistance=100 package=THT]
  R11 = Resistor [tolerance=±5% resistance=100 package=THT]
  Q6 = MOSFET-NCHANNEL [package=to-92]
  Q7 = MOSFET-NCHANNEL [package=to-92]
  Q8 = MOSFET-NCHANNEL [package=to-92]
  R12 = Resistor [tolerance=±5% resistance=10k package=THT]
  R13 = Resistor [tolerance=±5% resistance=10k package=THT]
  R14 = Resistor [tolerance=±5% resistance=10k package=THT]
  R15 = Resistor [tolerance=±5% resistance=100 package=THT]
  R16 = Resistor [tolerance=±5% resistance=100 package=THT]
  R17 = Resistor [tolerance=±5% resistance=100 package=THT]
  R5 = Resistor [tolerance=±5% resistance=100 package=THT]
  R20 = Resistor [tolerance=±5% resistance=100 package=THT]
  R21 = Resistor [tolerance=±5% resistance=10k package=THT]
  R22 = Resistor [tolerance=±5% resistance=10k package=THT]
  R23 = Resistor [tolerance=±5% resistance=4.7k package=THT]
  DS3 = DS18B20 1-Wire Temperature Sensor [part_number=DS18B20]
  DS4 = DS18B20 1-Wire Temperature Sensor [part_number=DS18B20]
  DS5 = DS18B20 1-Wire Temperature Sensor [part_number=DS18B20]
  RF_Jump = double row female pin header, 8 pins [form="♀ (female)"]
  GPS = female pin header, 6 pins [form="♀ (female)"]
  Compass = female pin header, 5 pins [form="♀ (female)"]
  GPS_Comms = female pin header, 5 pins [form="♀ (female)"]
  R25 = Resistor [tolerance=±5% resistance=10k package=THT]
  Photocell = female pin header, 2 pins [form="♀ (female)"]

nets:
  N1: Part1.A5, R25.Pin_0
  N2: Part1.D21/SCL, Part1.SCL, RTC.SCL, Compass.pin3
  N3: Part1.D20/SDA, Part1.SDA, RTC.SDA, Compass.pin2
  N4: Part1.D17_PWM/RX2, GPS_Comms.pin4
  N5: Part1.D16_PWM/TX2, GPS_Comms.pin3
  N6: Part1.D15/RX3, GPS.pin4
  N7: Part1.D14/TX3, GPS.pin3
  N8: Part1.GND, Q1.G, Q2.G, Q3.G, Q4.G, Q5.G, R6.Pin_1, R7.Pin_1, R8.Pin_1, Q6.G, Q7.G, Q8.G, R12.Pin_1, R13.Pin_1, R14.Pin_1, R21.Pin_1, R22.Pin_1, GPS_Comms.pin2, R25.Pin_1
  VDD: Part1.5V, DS2.VDD, RTC.5V, R23.Pin_0, DS3.VDD, DS4.VDD, DS5.VDD, RF_Jump.pin1, GPS.pin5, GPS_Comms.pin1, Photocell.pin2
  N9: Part1.D2_PWM, DS2.DQ, R23.Pin_1, DS3.DQ, DS4.DQ, DS5.DQ
  N10: Part1.D6_PWM, R5.Pin_0
  N11: Part1.D7_PWM, R9.Pin_0
  N12: Part1.D22, GPS_Comms.pin5
  N13: Part1.D27, R15.Pin_0
  N14: Part1.D32, R11.Pin_0
  N15: Part1.D38, R20.Pin_0
  N16: Part1.D42, R16.Pin_0
  N17: Part1.D46, R17.Pin_0
  N18: Part1.D47, R10.Pin_0
  N19: Part1.D49, RF_Jump.pin7
  N20: Part1.D50, RF_Jump.pin5
  N21: Part1.D51, RF_Jump.pin3
  N22: Part1.D52, RF_Jump.pin6
  N23: Part1.D53, RF_Jump.pin2
  N24: Q1.D, R20.Pin_1, R22.Pin_0
  N25: Q1.S, RTC.GND
  GND: DS2.GND, Q2.S, DS3.GND, DS4.GND, DS5.GND
  N26: Q2.D, R5.Pin_1, R21.Pin_0
  N27: Q3.D, R6.Pin_0, R9.Pin_1
  N28: Q3.S, GPS.pin2
  N29: Q4.D, R7.Pin_0, R10.Pin_1
  N30: Q4.S, RF_Jump.pin8
  N31: Q5.D, R8.Pin_0, R11.Pin_1
  N32: Q6.D, R12.Pin_0, R15.Pin_1
  N33: Q7.D, R13.Pin_0, R16.Pin_1
  N34: Q7.S, Photocell.pin1
  N35: Q8.D, R14.Pin_0, R17.Pin_1
